# Fritzing sketch schematics (saved by Fritzing 0.9.3b)

parts:
  Part1 = Arduino Uno (Rev3)
  M1 = DC Motor
  M2 = DC Motor
  S1 = H-Bridge with L298N
  J1 = Basic Servo
  VCC1 = Battery

nets:
  N1: Part1.A1, S1.IN4
  N2: Part1.A2, S1.IN3
  N3: Part1.D2, S1.IN1
  N4: Part1.D3_PWM, S1.ENB
  N5: Part1.D4, S1.IN2
  N6: Part1.D5_PWM, S1.ENA
  N7: Part1.D6_PWM, J1.pulse
  GND: Part1.GND, S1.GND, J1.gnd, VCC1.-
  VIN: Part1.VIN, S1.5V
  N8: M1.pin_1, S1.M1-02
  N9: M1.pin_2, S1.M1-01
  N10: M2.pin_1, S1.M2-02
  N11: M2.pin_2, S1.M2-01
  12V: S1.12V, J1.vcc, VCC1.+

custom parts:
  H-Bridge with L298N: h-bridge
